# Fritzing sketch Circuit scheme (saved by Fritzing 0.9.3b)
breadboards: 1

parts:
  DS1 = DS18B20 1-Wire Temperature Sensor [part_number=DS18B20]
  Componente1 = Arduino Uno (Rev3)
  R1 = Resistor [tolerance=±5% resistance=4.7k package=THT]
  T1 = LM35 Temperature Sensor [package="TO92 [THT]"]

nets:
  GND: DS1.GND, Componente1.GND, T1.GND
  N1: DS1.DQ, Componente1.D2, R1.Pin_1
  VDD: DS1.VDD, Componente1.5V, R1.Pin_0, T1.+Vs
  N2: Componente1.A0, T1.Vout
